# Fritzing sketch Schematic (saved by Fritzing 0.9.3b)
circuit board: 8.46667cm x 5.64444cm
breadboards: 1

parts:
  hc-sr1 = hc-sr04
  Part1 = Arduino Mega 2560 (Rev3)
  U1 = LCD-16X2 [package=lcd-16x2]
  J1 = Basic Servo
  HLK-PM1 = HLK-PM01
  R1 = Rotary Potentiometer (Large) [maximum_resistance=100kΩ package=THT]
  Q1 = NPN-Transistor [package="SOT-23 [SMD]"]
  M1 = DC Motor

nets:
  VCC: hc-sr1.VCC, U1.VDD, U1.A, J1.vcc, R1.leg2
  N1: hc-sr1.Echo, Part1.D35
  GND: hc-sr1.GND, U1.VSS, J1.gnd, R1.leg1
  N2: Part1.D13_PWM, Q1.0
  N3: Part1.D12_PWM, U1.DB6
  N4: Part1.D11_PWM, U1.DB5
  N5: Part1.D10_PWM, U1.DB4
  N6: Part1.D9_PWM, U1.DB3
  N7: Part1.D8_PWM, U1.DB2
  N8: Part1.D2_PWM, U1.VO
  N9: Part1.D3_PWM, U1.RS
  N10: Part1.D4_PWM, U1.R_W
  N11: Part1.D5_PWM, U1.E
  N12: Part1.D6_PWM, U1.DB0
  N13: Part1.D7_PWM, U1.DB1
  N14: Part1.D26, J1.pulse
  N15: U1.DB7, R1.wiper
  N16: HLK-PM1.-Vo, M1.pin_2
  N17: HLK-PM1.+Vo, Q1.1
  N18: Q1.2, M1.pin_1

custom parts:
  Basic Servo: A generic servo.

// code stored in the sketch: Fritzing... code.ino
#include <HCSR04.h>

#include <HCSR04.h>
 #include <Servo.h>
 
#define echoPin 35
#define trigPin 33
#define Grove_Water_Sensor 7 // Attach Water sensor to Arduino Digital Pin 7
#define LED 31// Attach an LED to Digital Pin 9 (or use onboard LED)
#include <LiquidCrystal.h> 
// initialize the library with the numbers of the interface pins
LiquidCrystal lcd(12,11,10,9,8,7,6,5,4,3,2);  
int pumpPin = 37; // water pump
int IRSensor = 28; // connect ir sensor to arduino pin 2
int distance;
long duration;

Servo myservo;  // create servo object to control a servo
// twelve servo objects can be created on most boards

int pos = 0;    // variable to store the servo position


void setup() {
  pinMode(trigPin,OUTPUT);
  pinMode (echoPin, INPUT);
  Serial.begin(9600);
  myservo.attach(24);  // attaches the servo on pin 24 to the servo object
   pinMode(LED, OUTPUT); // The LED is an Output
   pinMode(pumpPin, OUTPUT); //The pump is an Output
   pinMode (IRSensor, INPUT); // sensor pin INPUT
    lcd.begin(16,2);      // set up the LCD's number of columns and rows:

}

void loop() {
  digitalWrite(trigPin, LOW);
  delayMicroseconds(2);
  digitalWrite(trigPin, HIGH);
  delayMicroseconds(10);
  digitalWrite(trigPin, LOW);

  duration= pulseIn(echoPin, HIGH);
  distance= duration * 0.034 / 2;

  Serial.print( "Distance: ");
  Serial.print( distance);
  Serial.println ("cm");
 lcd.clear();
  lcd.setCursor(0,0);   // set the cursor to column 0, line 0
  lcd.print("Welcome, Please "); //// Print a message to the LCD.
  lcd.setCursor(0,2);   // set the cursor to column 0, line 2
  lcd.print("wash Your hands");  //Print a message to the LCD.
  /* The water sensor will switch LOW when water is detected.
   Get the Arduino to illuminate the LED and activate the buzzer
   when water is detected, and switch both off when no water is present */
   if(distance <= 5)
   {
      digitalWrite(LED,HIGH);
      digitalWrite(pumpPin,HIGH);
      
  //delay(15);
  lcd.clear();
  lcd.setCursor(0,0);   // set the cursor to column 0, line 0
  lcd.print("Washing hands  "); //// Print a message to the LCD.
  lcd.setCursor(0,2);   // set the cursor to column 0, line 2
  lcd.print("please wait.....");  //Print a message to the LCD.
   delay (2000);
      
   }else {
      digitalWrite(LED,LOW);
      digitalWrite(pumpPin,LOW);
      delay (1000);
  
   }

int statusSensor = digitalRead (IRSensor);
  
 // if (statusSensor == 1)
  if (distance >5 && distance <= 25)
   { myservo.write(180);              // tell servo to go to position in variable 'pos'
    delay(15);                       // waits 15ms for the servo to reach the position
 lcd.clear() ; 
  lcd.setCursor(0,0);   // set the cursor to column 0, line 0
  lcd.print("please proceed"); //// Print a message to the LCD.
  lcd.setCursor(0,2);   // set the cursor to column 0, line 2
  lcd.print("Now proceed...");  //Print a message to the LCD.
  delay(2000);
   }
    
//  for (pos = 180; pos >= 0; pos -= 1) { // goes from 180 degrees to 0 degrees
 
 else{
 myservo.write(0);              // tell servo to go to position in variable 'pos'
 delay(15);                       // waits 15ms for the servo to reach the position
 }   
 //   myservo.write(0);
 
 // lcd.clear();
 // lcd.setCursor(0,0);   // set the cursor to column 0, line 0
 // lcd.print("Welcome, Please "); //// Print a message to the LCD.
  lcd.setCursor(0,2);   // set the cursor to column 0, line 2
  lcd.print("wash Your hands");  //Print a message to the LCD.
}
